// Logisim project Main.circ as structural Verilog: 8 circuits, main circuit main
module main (
);

  wire boot_controller_1_primer_ciclo, boot_controller_1_reloj, clock_1_out, switch_1_p2;
  wire [31:0] if_controller_1_indice, if_controller_1_instruccion;

  // Switch switch_1: pin names not known; wires that end beside it: 1'b1, switch_1_p2
  Pull_Resistor pull_resistor_1 (.node(switch_1_p2));
  Clock clock_1 (.out(clock_1_out));
  Boot_Controller boot_controller_1 (
    .Reloj_Externo(clock_1_out), .Interruptor(switch_1_p2), .Primer_Ciclo(boot_controller_1_primer_ciclo),
    .Reloj(boot_controller_1_reloj));
  Hex_Digit_Display #(.decimalPoint("false")) hex_digit_display_1 (.value(if_controller_1_instruccion[31:28]));
  Hex_Digit_Display #(.decimalPoint("false")) hex_digit_display_2 (.value(if_controller_1_indice[31:28]));
  IF_Controller if_controller_1 (
    .Indice_Salto({32{1'b0}}), .Saltar(1'b0), .Dormir(1'b0), .Reloj(boot_controller_1_reloj),
    .Reiniciar(boot_controller_1_primer_ciclo), .Usar_Little_Endian(1'b0), .Indice(if_controller_1_indice),
    .Instruccion(if_controller_1_instruccion));  // open: Doble_Instruccion, Media_Instruccion, Cuarto_Instruccion
  Hex_Digit_Display #(.decimalPoint("false")) hex_digit_display_3 (.value(if_controller_1_instruccion[27:24]));
  Hex_Digit_Display #(.decimalPoint("false")) hex_digit_display_4 (.value(if_controller_1_instruccion[23:20]));
  Hex_Digit_Display #(.decimalPoint("false")) hex_digit_display_5 (.value(if_controller_1_indice[27:24]));
  Hex_Digit_Display #(.decimalPoint("false")) hex_digit_display_6 (.value(if_controller_1_indice[23:20]));
  Hex_Digit_Display #(.decimalPoint("false")) hex_digit_display_7 (.value(if_controller_1_instruccion[19:16]));
  Hex_Digit_Display #(.decimalPoint("false")) hex_digit_display_8 (.value(if_controller_1_instruccion[15:12]));
  Hex_Digit_Display #(.decimalPoint("false")) hex_digit_display_9 (.value(if_controller_1_indice[19:16]));
  Hex_Digit_Display #(.decimalPoint("false")) hex_digit_display_10 (.value(if_controller_1_indice[15:12]));
  Hex_Digit_Display #(.decimalPoint("false")) hex_digit_display_11 (.value(if_controller_1_instruccion[11:8]));
  Hex_Digit_Display #(.decimalPoint("false")) hex_digit_display_12 (.value(if_controller_1_instruccion[7:4]));
  Hex_Digit_Display #(.decimalPoint("false")) hex_digit_display_13 (.value(if_controller_1_indice[11:8]));
  Hex_Digit_Display #(.decimalPoint("false")) hex_digit_display_14 (.value(if_controller_1_indice[7:4]));
  Hex_Digit_Display #(.decimalPoint("false")) hex_digit_display_15 (.value(if_controller_1_instruccion[3:0]));
  Hex_Digit_Display #(.decimalPoint("false")) hex_digit_display_16 (.value(if_controller_1_indice[3:0]));

  // Notes on the sheet:
  //   Encender computadora
endmodule

module Boot_Controller (
  input  Reloj_Externo,
  input  Interruptor,
  output Primer_Ciclo,
  output Reloj
);

  wire and_1_out, d_ff_1_q, d_ff_1_qn, not_1_out, t_ff_1_q, t_ff_1_qn;

  T_Flip_Flop t_ff_1 (
    .T(t_ff_1_qn), .clk(Reloj_Externo), .Q(t_ff_1_q), .Qn(t_ff_1_qn), .reset(not_1_out), .preset(1'b0));
  not not_1 (not_1_out, Interruptor);
  and and_1 (and_1_out, Reloj_Externo, Interruptor);
  and and_2 (Reloj, t_ff_1_q, and_1_out);
  D_Flip_Flop d_ff_1 (
    .D(t_ff_1_qn), .clk(Reloj_Externo), .Q(d_ff_1_q), .Qn(d_ff_1_qn), .preset(1'b0), .reset(not_1_out));
  // NoConnect on d_ff_1_qn
  and and_3 (Primer_Ciclo, d_ff_1_q, Reloj);
endmodule

module Four_GB_ROM_Controller (
  input  [31:0] Direccion_32_bits,
  input  Usar_Litte_Endian,
  output [63:0] Doubleword,
  output [31:0] Word,
  output [15:0] Nibble,
  output [7:0] Byte
);

  wire [2:0] subtractor_2_out;
  wire [31:0] multiplexer_1_out, subtractor_1_out;
  wire [63:0] multiplexer_2_out, multiplexer_3_out, rom_1_data, rom_2_data, rom_3_data, rom_4_data,
       rom_5_data, rom_6_data, rom_7_data, rom_8_data, rom_9_data, rom_10_data, rom_11_data, rom_12_data,
       rom_13_data, rom_14_data, rom_15_data, rom_16_data, rom_17_data, rom_18_data, rom_19_data,
       rom_20_data, rom_21_data, rom_22_data, rom_23_data, rom_24_data, rom_25_data, rom_26_data,
       rom_27_data, rom_28_data, rom_29_data, rom_30_data, rom_31_data, rom_32_data;

  Subtractor #(.width(32)) subtractor_1 (
    .a({32{1'b1}}), .b(Direccion_32_bits), .out(subtractor_1_out), .bin(1'b0));  // open: bout
  Multiplexer #(.width(32)) multiplexer_1 (
    .in0(Direccion_32_bits), .in1(subtractor_1_out), .out(multiplexer_1_out), .sel(Usar_Litte_Endian));
  Subtractor #(.width(3)) subtractor_2 (
    .a(3'b111), .b(multiplexer_1_out[2:0]), .out(subtractor_2_out), .bin(1'b0));  // open: bout
  ROM #(.addrWidth(24), .dataWidth(64)) rom_1 (.addr(multiplexer_1_out[26:3]), .data(rom_1_data));
  ROM #(.addrWidth(24), .dataWidth(64)) rom_2 (.addr(multiplexer_1_out[26:3]), .data(rom_2_data));
  ROM #(.addrWidth(24), .dataWidth(64)) rom_3 (.addr(multiplexer_1_out[26:3]), .data(rom_3_data));
  ROM #(.addrWidth(24), .dataWidth(64)) rom_4 (.addr(multiplexer_1_out[26:3]), .data(rom_4_data));
  ROM #(.addrWidth(24), .dataWidth(64)) rom_5 (.addr(multiplexer_1_out[26:3]), .data(rom_5_data));
  ROM #(.addrWidth(24), .dataWidth(64)) rom_6 (.addr(multiplexer_1_out[26:3]), .data(rom_6_data));
  ROM #(.addrWidth(24), .dataWidth(64)) rom_7 (.addr(multiplexer_1_out[26:3]), .data(rom_7_data));
  ROM #(.addrWidth(24), .dataWidth(64)) rom_8 (.addr(multiplexer_1_out[26:3]), .data(rom_8_data));
  ROM #(.addrWidth(24), .dataWidth(64)) rom_9 (.addr(multiplexer_1_out[26:3]), .data(rom_9_data));
  ROM #(.addrWidth(24), .dataWidth(64)) rom_10 (.addr(multiplexer_1_out[26:3]), .data(rom_10_data));
  ROM #(.addrWidth(24), .dataWidth(64)) rom_11 (.addr(multiplexer_1_out[26:3]), .data(rom_11_data));
  ROM #(.addrWidth(24), .dataWidth(64)) rom_12 (.addr(multiplexer_1_out[26:3]), .data(rom_12_data));
  ROM #(.addrWidth(24), .dataWidth(64)) rom_13 (.addr(multiplexer_1_out[26:3]), .data(rom_13_data));
  ROM #(.addrWidth(24), .dataWidth(64)) rom_14 (.addr(multiplexer_1_out[26:3]), .data(rom_14_data));
  ROM #(.addrWidth(24), .dataWidth(64)) rom_15 (.addr(multiplexer_1_out[26:3]), .data(rom_15_data));
  ROM #(.addrWidth(24), .dataWidth(64)) rom_16 (.addr(multiplexer_1_out[26:3]), .data(rom_16_data));
  ROM #(.addrWidth(24), .dataWidth(64)) rom_17 (.addr(multiplexer_1_out[26:3]), .data(rom_17_data));
  ROM #(.addrWidth(24), .dataWidth(64)) rom_18 (.addr(multiplexer_1_out[26:3]), .data(rom_18_data));
  ROM #(.addrWidth(24), .dataWidth(64)) rom_19 (.addr(multiplexer_1_out[26:3]), .data(rom_19_data));
  ROM #(.addrWidth(24), .dataWidth(64)) rom_20 (.addr(multiplexer_1_out[26:3]), .data(rom_20_data));
  ROM #(.addrWidth(24), .dataWidth(64)) rom_21 (.addr(multiplexer_1_out[26:3]), .data(rom_21_data));
  ROM #(.addrWidth(24), .dataWidth(64)) rom_22 (.addr(multiplexer_1_out[26:3]), .data(rom_22_data));
  ROM #(.addrWidth(24), .dataWidth(64)) rom_23 (.addr(multiplexer_1_out[26:3]), .data(rom_23_data));
  ROM #(.addrWidth(24), .dataWidth(64)) rom_24 (.addr(multiplexer_1_out[26:3]), .data(rom_24_data));
  ROM #(.addrWidth(24), .dataWidth(64)) rom_25 (.addr(multiplexer_1_out[26:3]), .data(rom_25_data));
  ROM #(.addrWidth(24), .dataWidth(64)) rom_26 (.addr(multiplexer_1_out[26:3]), .data(rom_26_data));
  ROM #(.addrWidth(24), .dataWidth(64)) rom_27 (.addr(multiplexer_1_out[26:3]), .data(rom_27_data));
  ROM #(.addrWidth(24), .dataWidth(64)) rom_28 (.addr(multiplexer_1_out[26:3]), .data(rom_28_data));
  ROM #(.addrWidth(24), .dataWidth(64)) rom_29 (.addr(multiplexer_1_out[26:3]), .data(rom_29_data));
  ROM #(.addrWidth(24), .dataWidth(64)) rom_30 (.addr(multiplexer_1_out[26:3]), .data(rom_30_data));
  ROM #(.addrWidth(24), .dataWidth(64)) rom_31 (.addr(multiplexer_1_out[26:3]), .data(rom_31_data));
  ROM #(.addrWidth(24), .dataWidth(64)) rom_32 (.addr(multiplexer_1_out[26:3]), .data(rom_32_data));
  Multiplexer #(.select(4), .width(64)) multiplexer_2 (
    .in0(rom_1_data), .in1(rom_2_data), .in2(rom_3_data), .in3(rom_4_data), .in4(rom_9_data),
    .in5(rom_10_data), .in6(rom_11_data), .in7(rom_12_data), .in8(rom_17_data), .in9(rom_18_data),
    .in10(rom_19_data), .in11(rom_20_data), .in12(rom_25_data), .in13(rom_26_data), .in14(rom_27_data),
    .in15(rom_28_data), .out(multiplexer_2_out), .sel(multiplexer_1_out[30:27]));
  Multiplexer #(.select(4), .width(64)) multiplexer_3 (
    .in0(rom_5_data), .in1(rom_6_data), .in2(rom_7_data), .in3(rom_8_data), .in4(rom_13_data),
    .in5(rom_14_data), .in6(rom_15_data), .in7(rom_16_data), .in8(rom_21_data), .in9(rom_22_data),
    .in10(rom_23_data), .in11(rom_24_data), .in12(rom_29_data), .in13(rom_30_data), .in14(rom_31_data),
    .in15(rom_32_data), .out(multiplexer_3_out), .sel(multiplexer_1_out[30:27]));
  Multiplexer #(.width(64)) multiplexer_4 (
    .in0(multiplexer_2_out), .in1(multiplexer_3_out), .out(Doubleword), .sel(multiplexer_1_out[31]));
  Multiplexer #(.width(32)) multiplexer_5 (
    .in0(Doubleword[31:0]), .in1(Doubleword[63:32]), .out(Word), .sel(subtractor_2_out[2]));
  Multiplexer #(.width(16)) multiplexer_6 (
    .in0(Word[15:0]), .in1(Word[31:16]), .out(Nibble), .sel(subtractor_2_out[1]));
  Multiplexer #(.width(8)) multiplexer_7 (.in0(Nibble[7:0]), .in1(Nibble[15:8]), .out(Byte), .sel(subtractor_2_out[0]));

  // Notes on the sheet:
  //   Tamaño de memoria accesible
  //   Longitud de byte
  //   contents of rom_1 (hex, n*v repeats v):
  //   123456789abcdef fedcba9876543210
  //   4 Gigabit
  //   4 Gigabit
  //   4 Gigabit
  //   4 Gigabit
  //   4 Gigabytes
  //   4 Giganibbles
  //   4 Giganibbles
  //   4 Gigabit
  //   4 Gigabit
  //   contents of rom_32 (hex, n*v repeats v):
  //   16777215*0 123456789abcdef
  //   4 Gigabit
  //   4 Gigabit
endmodule

module PC_Controller (
  input  [31:0] Indice_Salto,
  input  Tomar_Salto,
  input  Dormir,
  input  Reloj,
  input  Reiniciar,
  output [31:0] Indice
);

  wire not_1_out, not_2_out;
  wire [31:0] adder_1_out, multiplexer_1_out;

  not not_1 (not_1_out, Tomar_Salto);
  Multiplexer #(.width(32)) multiplexer_1 (
    .in0(Indice_Salto), .in1(adder_1_out), .out(multiplexer_1_out), .sel(not_1_out));
  not not_2 (not_2_out, Dormir);
  Register #(.width(32)) PC (.D(multiplexer_1_out), .en(not_2_out), .clk(Reloj), .Q(Indice), .clr(Reiniciar));
  Adder #(.width(32)) adder_1 (.a(32'h4), .b(Indice), .out(adder_1_out), .cin(1'b0));  // open: cout

  // Notes on the sheet:
  //   Alienamiento de Instrucciones
endmodule

module IF_Controller (
  input  [31:0] Indice_Salto,
  input  Saltar,
  input  Dormir,
  input  Reloj,
  input  Reiniciar,
  input  Usar_Little_Endian,
  output [31:0] Indice,
  output [63:0] Doble_Instruccion,
  output [31:0] Instruccion,
  output [15:0] Media_Instruccion,
  output [7:0] Cuarto_Instruccion
);

  PC_Controller pc_controller_1 (
    .Indice_Salto(Indice_Salto), .Tomar_Salto(Saltar), .Dormir(Dormir), .Reloj(Reloj), .Reiniciar(Reiniciar),
    .Indice(Indice));
  Four_GB_ROM_Controller four_gb_rom_controller_1 (
    .Direccion_32_bits(Indice), .Usar_Litte_Endian(Usar_Little_Endian), .Doubleword(Doble_Instruccion),
    .Word(Instruccion), .Nibble(Media_Instruccion), .Byte(Cuarto_Instruccion));
endmodule

module Instruction_Decoder (
  input  [31:0] Instruccion,
  output [6:0] Funcion_Aritmetica,
  output [4:0] Cantidad_Corrimiento,
  output [4:0] Registro_Destino,
  output [15:0] Valor_Inmediato,
  output [4:0] Registro_Temporal,
  output [4:0] Registro_Fuente,
  output [25:0] Direccion,
  output Tipo_I,
  output Tipo_J,
  output Tipo_R
);

  wire comparator_1_eq, comparator_2_eq;

  Comparator #(.mode("unsigned"), .width(6)) comparator_1 (
    .a(Instruccion[31:26]), .b(6'b000011), .gt(Tipo_I), .eq(comparator_1_eq));  // open: lt
  Comparator #(.mode("unsigned"), .width(6)) comparator_2 (
    .a(6'b000010), .b(Instruccion[31:26]), .eq(comparator_2_eq));  // open: gt, lt
  Comparator #(.mode("unsigned"), .width(6)) comparator_3 (
    .a({6{1'b0}}), .b(Instruccion[31:26]), .eq(Tipo_R));  // open: gt, lt
  or or_1 (Tipo_J, comparator_1_eq, comparator_2_eq);

  assign Cantidad_Corrimiento = Instruccion[11:7];
  assign Direccion = Instruccion[25:0];
  assign Funcion_Aritmetica = Instruccion[6:0];
  assign Registro_Destino = Instruccion[16:12];
  assign Registro_Fuente = Instruccion[25:21];
  assign Registro_Temporal = Instruccion[20:16];
  assign Valor_Inmediato = Instruccion[15:0];
endmodule

module Register_File_Controller (
  input  Limpiar,
  input  [4:0] Indice_Registro,
  input  Bloquear,
  input  Escribir,
  input  Reloj,
  input  [31:0] Entrada,
  output [31:0] Salida
);

  wire and_1_out, and_2_out;

  and and_1 (and_1_out, ~Escribir, ~Bloquear);  // AND_Gate
  RAM #(.addrWidth(5), .clearpin("true"), .dataWidth(32)) Pagina_de_Registros (
    .addr(Indice_Registro), .we(and_2_out), .oe(and_1_out), .clk(Reloj), .din(Entrada), .dout(Salida),
    .clr(Limpiar));
  and and_2 (and_2_out, Escribir, ~Bloquear);  // AND_Gate
endmodule

module Four_GB_RAM_Controller (
  input  Reloj,
  input  Limpiar,
  input  Bloquear,
  input  Escribir,
  input  [31:0] Direccion_32_bits,
  input  Usar_Litte_Endian,
  input  [31:0] Entrada,
  output [63:0] Doubleword,
  output [31:0] Word,
  output [15:0] Nibble,
  output [7:0] Byte
);

  wire and_1_out, and_2_out, and_3_out, and_4_out, and_5_out, and_6_out, and_7_out, and_8_out, and_9_out,
       and_10_out, and_11_out, and_12_out, and_13_out, and_14_out, and_15_out, and_16_out, and_17_out,
       and_18_out, and_19_out, and_20_out, and_21_out, and_22_out, and_23_out, and_24_out, and_25_out,
       and_26_out, and_27_out, and_28_out, and_30_out, and_31_out, and_32_out, and_33_out, and_34_out,
       and_35_out, and_36_out, and_37_out, and_38_out, and_39_out, and_40_out, and_41_out, and_42_out,
       and_43_out, and_44_out, and_45_out, and_46_out, and_47_out, and_48_out, and_49_out, and_50_out,
       and_51_out, and_52_out, and_53_out, and_54_out, and_55_out, and_56_out, and_57_out, and_58_out,
       and_59_out, and_60_out, and_61_out, and_62_out, and_63_out, and_64_out, and_65_out, and_66_out,
       and_67_out, and_68_out, and_69_out, and_70_out, and_71_out, and_72_out, and_73_out, and_74_out,
       and_75_out, and_76_out, and_77_out, and_78_out, and_79_out, and_80_out, and_81_out, and_82_out,
       and_83_out, and_84_out, and_85_out, and_86_out, and_87_out, and_88_out, and_89_out, and_90_out,
       and_91_out, and_92_out, and_93_out, and_94_out, and_95_out, and_96_out, and_97_out, and_98_out,
       and_99_out, and_100_out, and_101_out, and_102_out, and_103_out, decoder_1_out0, decoder_1_out1,
       decoder_2_out0, decoder_2_out1, decoder_2_out2, decoder_2_out3, decoder_3_out0, decoder_3_out1,
       decoder_3_out2, decoder_3_out3, decoder_4_out0, decoder_4_out1, decoder_4_out2, decoder_4_out3,
       decoder_5_out0, decoder_5_out1, decoder_5_out2, decoder_5_out3;
  wire [1:0] multiplexer_1_out_3, multiplexer_1_out_4;
  wire [2:0] subtractor_2_out;
  wire [5:0] multiplexer_5_out;
  wire [23:0] multiplexer_1_out_2;
  wire [31:0] multiplexer_1_out, subtractor_1_out;
  wire [63:0] and_29_out, bit_extender_1_out, controlled_buffer_1_out, controlled_buffer_18_out,
       multiplexer_6_out, not_1_out, or_1_out, ram_1_dout, ram_2_dout, ram_3_dout, ram_4_dout, ram_5_dout,
       ram_6_dout, ram_7_dout, ram_8_dout, ram_9_dout, ram_10_dout, ram_11_dout, ram_12_dout, ram_13_dout,
       ram_14_dout, ram_15_dout, ram_16_dout, ram_17_dout, ram_18_dout, ram_19_dout, ram_20_dout,
       ram_21_dout, ram_22_dout, ram_23_dout, ram_24_dout, ram_25_dout, ram_26_dout, ram_27_dout,
       ram_28_dout, ram_29_dout, ram_30_dout, ram_31_dout, ram_32_dout, shifter_1_out;

  Subtractor #(.width(32)) subtractor_1 (
    .a({32{1'b1}}), .b(Direccion_32_bits), .out(subtractor_1_out), .bin(1'b0));  // open: bout
  Multiplexer #(.width(32)) multiplexer_1 (
    .in0(Direccion_32_bits), .in1(subtractor_1_out),
    .out({multiplexer_1_out[31], multiplexer_1_out_4, multiplexer_1_out_3, multiplexer_1_out_2, multiplexer_1_out[2:0]}),
    .sel(Usar_Litte_Endian));
  Subtractor #(.width(3)) subtractor_2 (
    .a(3'b111), .b(multiplexer_1_out[2:0]), .out(subtractor_2_out), .bin(1'b0));  // open: bout
  // Probe on subtractor_2_out
  and and_1 (and_1_out, ~Escribir, ~Bloquear);  // AND_Gate
  and and_2 (and_2_out, Escribir, ~Bloquear);  // AND_Gate
  Decoder #(.enable("false")) decoder_1 (.out0(decoder_1_out0), .out1(decoder_1_out1), .sel(multiplexer_1_out[31]));
  // Probe on multiplexer_1_out_2
  // Probe on multiplexer_1_out_4
  // Probe on multiplexer_1_out_3
  and and_3 (and_3_out, decoder_1_out0, and_2_out);
  and and_4 (and_4_out, decoder_1_out0, and_1_out);
  // Probe on {multiplexer_1_out_4, multiplexer_1_out_3, multiplexer_1_out_2}
  Decoder #(.enable("false"), .select(2)) decoder_2 (
    .out0(decoder_2_out0), .out1(decoder_2_out1), .out2(decoder_2_out2), .out3(decoder_2_out3),
    .sel(multiplexer_1_out_4));
  Decoder #(.enable("false"), .select(2)) decoder_3 (
    .out0(decoder_3_out0), .out1(decoder_3_out1), .out2(decoder_3_out2), .out3(decoder_3_out3),
    .sel(multiplexer_1_out_3));
  and and_5 (and_5_out, decoder_3_out0, decoder_2_out0);
  and and_6 (and_6_out, and_5_out, and_3_out);
  and and_7 (and_7_out, and_5_out, and_4_out);
  and and_8 (and_8_out, decoder_3_out0, decoder_2_out1);
  and and_9 (and_9_out, and_8_out, and_3_out);
  and and_10 (and_10_out, and_8_out, and_4_out);
  and and_11 (and_11_out, decoder_3_out0, decoder_2_out2);
  and and_12 (and_12_out, and_11_out, and_3_out);
  and and_13 (and_13_out, and_11_out, and_4_out);
  and and_14 (and_14_out, decoder_3_out0, decoder_2_out3);
  and and_15 (and_15_out, and_14_out, and_3_out);
  and and_16 (and_16_out, and_14_out, and_4_out);
  RAM #(.addrWidth(24), .clearpin("true"), .dataWidth(64)) ram_1 (
    .addr(multiplexer_1_out_2), .we(and_6_out), .oe(and_7_out), .clk(Reloj), .din(or_1_out),
    .dout(ram_1_dout), .clr(Limpiar));
  RAM #(.addrWidth(24), .clearpin("true"), .dataWidth(64)) ram_2 (
    .addr(multiplexer_1_out_2), .we(and_9_out), .oe(and_10_out), .clk(Reloj), .din(or_1_out),
    .dout(ram_2_dout), .clr(Limpiar));
  RAM #(.addrWidth(24), .clearpin("true"), .dataWidth(64)) ram_3 (
    .addr(multiplexer_1_out_2), .we(and_12_out), .oe(and_13_out), .clk(Reloj), .din(or_1_out),
    .dout(ram_3_dout), .clr(Limpiar));
  RAM #(.addrWidth(24), .clearpin("true"), .dataWidth(64)) ram_4 (
    .addr(multiplexer_1_out_2), .we(and_15_out), .oe(and_16_out), .clk(Reloj), .din(or_1_out),
    .dout(ram_4_dout), .clr(Limpiar));
  assign controlled_buffer_1_out = and_5_out ? ram_1_dout : 64'bz;  // Controlled_Buffer controlled_buffer_1
  assign controlled_buffer_1_out = and_8_out ? ram_2_dout : 64'bz;  // Controlled_Buffer controlled_buffer_2
  assign controlled_buffer_1_out = and_11_out ? ram_3_dout : 64'bz;  // Controlled_Buffer controlled_buffer_3
  assign controlled_buffer_1_out = and_14_out ? ram_4_dout : 64'bz;  // Controlled_Buffer controlled_buffer_4
  assign Doubleword = decoder_1_out0 ? controlled_buffer_1_out : 64'bz;  // Controlled_Buffer controlled_buffer_5
  and and_17 (and_17_out, decoder_3_out1, decoder_2_out0);
  and and_18 (and_18_out, decoder_3_out1, decoder_2_out1);
  and and_19 (and_19_out, decoder_3_out1, decoder_2_out2);
  and and_20 (and_20_out, decoder_3_out1, decoder_2_out3);
  Multiplexer #(.width(32)) multiplexer_2 (
    .in0(Doubleword[31:0]), .in1(Doubleword[63:32]), .out(Word), .sel(subtractor_2_out[2]));
  and and_21 (and_21_out, and_17_out, and_3_out);
  and and_22 (and_22_out, and_17_out, and_4_out);
  and and_23 (and_23_out, and_18_out, and_3_out);
  and and_24 (and_24_out, and_18_out, and_4_out);
  and and_25 (and_25_out, and_19_out, and_3_out);
  and and_26 (and_26_out, and_19_out, and_4_out);
  and and_27 (and_27_out, and_20_out, and_3_out);
  and and_28 (and_28_out, and_20_out, and_4_out);
  Multiplexer #(.width(16)) multiplexer_3 (
    .in0(Word[15:0]), .in1(Word[31:16]), .out(Nibble), .sel(subtractor_2_out[1]));
  Multiplexer #(.width(8)) multiplexer_4 (.in0(Nibble[7:0]), .in1(Nibble[15:8]), .out(Byte), .sel(subtractor_2_out[0]));
  assign bit_extender_1_out = {{32{1'b0}}, Entrada};  // Bit_Extender bit_extender_1
  Multiplexer #(.width(6)) multiplexer_5 (
    .in0({6{1'b0}}), .in1(6'b100000), .out(multiplexer_5_out), .sel(subtractor_2_out[2]));
  RAM #(.addrWidth(24), .clearpin("true"), .dataWidth(64)) ram_5 (
    .addr(multiplexer_1_out_2), .we(and_21_out), .oe(and_22_out), .clk(Reloj), .din(or_1_out),
    .dout(ram_5_dout), .clr(Limpiar));
  RAM #(.addrWidth(24), .clearpin("true"), .dataWidth(64)) ram_6 (
    .addr(multiplexer_1_out_2), .we(and_23_out), .oe(and_24_out), .clk(Reloj), .din(or_1_out),
    .dout(ram_6_dout), .clr(Limpiar));
  RAM #(.addrWidth(24), .clearpin("true"), .dataWidth(64)) ram_7 (
    .addr(multiplexer_1_out_2), .we(and_25_out), .oe(and_26_out), .clk(Reloj), .din(or_1_out),
    .dout(ram_7_dout), .clr(Limpiar));
  RAM #(.addrWidth(24), .clearpin("true"), .dataWidth(64)) ram_8 (
    .addr(multiplexer_1_out_2), .we(and_27_out), .oe(and_28_out), .clk(Reloj), .din(or_1_out),
    .dout(ram_8_dout), .clr(Limpiar));
  assign not_1_out = ~64'hffffffff;  // NOT_Gate not_1, 64 bits wide
  Shifter #(.width(64)) shifter_1 (.in(bit_extender_1_out), .\dist (multiplexer_5_out), .out(shifter_1_out));
  assign and_29_out = Doubleword & multiplexer_6_out;  // AND_Gate and_29, 64 bits wide
  Multiplexer #(.width(64)) multiplexer_6 (
    .in0(not_1_out), .in1(64'hffffffff), .out(multiplexer_6_out), .sel(subtractor_2_out[2]));
  assign or_1_out = and_29_out | shifter_1_out;  // OR_Gate or_1, 64 bits wide
  // Probe on or_1_out
  assign controlled_buffer_1_out = and_17_out ? ram_5_dout : 64'bz;  // Controlled_Buffer controlled_buffer_6
  assign controlled_buffer_1_out = and_18_out ? ram_6_dout : 64'bz;  // Controlled_Buffer controlled_buffer_7
  assign controlled_buffer_1_out = and_19_out ? ram_7_dout : 64'bz;  // Controlled_Buffer controlled_buffer_8
  assign controlled_buffer_1_out = and_20_out ? ram_8_dout : 64'bz;  // Controlled_Buffer controlled_buffer_9
  and and_30 (and_30_out, decoder_3_out2, decoder_2_out0);
  and and_31 (and_31_out, decoder_3_out2, decoder_2_out1);
  and and_32 (and_32_out, decoder_3_out2, decoder_2_out2);
  and and_33 (and_33_out, decoder_3_out2, decoder_2_out3);
  RAM #(.addrWidth(24), .clearpin("true"), .dataWidth(64)) ram_9 (
    .addr(multiplexer_1_out_2), .we(and_34_out), .oe(and_35_out), .clk(Reloj), .din(or_1_out),
    .dout(ram_9_dout), .clr(Limpiar));
  and and_34 (and_34_out, and_30_out, and_3_out);
  and and_35 (and_35_out, and_30_out, and_4_out);
  RAM #(.addrWidth(24), .clearpin("true"), .dataWidth(64)) ram_10 (
    .addr(multiplexer_1_out_2), .we(and_36_out), .oe(and_37_out), .clk(Reloj), .din(or_1_out),
    .dout(ram_10_dout), .clr(Limpiar));
  and and_36 (and_36_out, and_31_out, and_3_out);
  and and_37 (and_37_out, and_31_out, and_4_out);
  RAM #(.addrWidth(24), .clearpin("true"), .dataWidth(64)) ram_11 (
    .addr(multiplexer_1_out_2), .we(and_38_out), .oe(and_39_out), .clk(Reloj), .din(or_1_out),
    .dout(ram_11_dout), .clr(Limpiar));
  and and_38 (and_38_out, and_32_out, and_3_out);
  and and_39 (and_39_out, and_32_out, and_4_out);
  RAM #(.addrWidth(24), .clearpin("true"), .dataWidth(64)) ram_12 (
    .addr(multiplexer_1_out_2), .we(and_40_out), .oe(and_41_out), .clk(Reloj), .din(or_1_out),
    .dout(ram_12_dout), .clr(Limpiar));
  and and_40 (and_40_out, and_33_out, and_3_out);
  and and_41 (and_41_out, and_33_out, and_4_out);
  and and_42 (and_42_out, decoder_3_out3, decoder_2_out0);
  assign controlled_buffer_1_out = and_30_out ? ram_9_dout : 64'bz;  // Controlled_Buffer controlled_buffer_10
  and and_43 (and_43_out, decoder_3_out3, decoder_2_out1);
  assign controlled_buffer_1_out = and_31_out ? ram_10_dout : 64'bz;  // Controlled_Buffer controlled_buffer_11
  and and_44 (and_44_out, decoder_3_out3, decoder_2_out2);
  assign controlled_buffer_1_out = and_32_out ? ram_11_dout : 64'bz;  // Controlled_Buffer controlled_buffer_12
  and and_45 (and_45_out, decoder_3_out3, decoder_2_out3);
  assign controlled_buffer_1_out = and_33_out ? ram_12_dout : 64'bz;  // Controlled_Buffer controlled_buffer_13
  and and_46 (and_46_out, and_42_out, and_3_out);
  and and_47 (and_47_out, and_42_out, and_4_out);
  and and_48 (and_48_out, and_43_out, and_3_out);
  and and_49 (and_49_out, and_43_out, and_4_out);
  and and_50 (and_50_out, and_44_out, and_3_out);
  and and_51 (and_51_out, and_44_out, and_4_out);
  and and_52 (and_52_out, and_45_out, and_3_out);
  and and_53 (and_53_out, and_45_out, and_4_out);
  RAM #(.addrWidth(24), .clearpin("true"), .dataWidth(64)) ram_13 (
    .addr(multiplexer_1_out_2), .we(and_46_out), .oe(and_47_out), .clk(Reloj), .din(or_1_out),
    .dout(ram_13_dout), .clr(Limpiar));
  RAM #(.addrWidth(24), .clearpin("true"), .dataWidth(64)) ram_14 (
    .addr(multiplexer_1_out_2), .we(and_48_out), .oe(and_49_out), .clk(Reloj), .din(or_1_out),
    .dout(ram_14_dout), .clr(Limpiar));
  RAM #(.addrWidth(24), .clearpin("true"), .dataWidth(64)) ram_15 (
    .addr(multiplexer_1_out_2), .we(and_50_out), .oe(and_51_out), .clk(Reloj), .din(or_1_out),
    .dout(ram_15_dout), .clr(Limpiar));
  RAM #(.addrWidth(24), .clearpin("true"), .dataWidth(64)) ram_16 (
    .addr(multiplexer_1_out_2), .we(and_52_out), .oe(and_53_out), .clk(Reloj), .din(or_1_out),
    .dout(ram_16_dout), .clr(Limpiar));
  assign controlled_buffer_1_out = and_42_out ? ram_13_dout : 64'bz;  // Controlled_Buffer controlled_buffer_14
  assign controlled_buffer_1_out = and_43_out ? ram_14_dout : 64'bz;  // Controlled_Buffer controlled_buffer_15
  assign controlled_buffer_1_out = and_44_out ? ram_15_dout : 64'bz;  // Controlled_Buffer controlled_buffer_16
  assign controlled_buffer_1_out = and_45_out ? ram_16_dout : 64'bz;  // Controlled_Buffer controlled_buffer_17
  and and_54 (and_54_out, decoder_1_out1, and_2_out);
  and and_55 (and_55_out, decoder_1_out1, and_1_out);
  Decoder #(.enable("false"), .select(2)) decoder_4 (
    .out0(decoder_4_out0), .out1(decoder_4_out1), .out2(decoder_4_out2), .out3(decoder_4_out3),
    .sel(multiplexer_1_out_4));
  Decoder #(.enable("false"), .select(2)) decoder_5 (
    .out0(decoder_5_out0), .out1(decoder_5_out1), .out2(decoder_5_out2), .out3(decoder_5_out3),
    .sel(multiplexer_1_out_3));
  and and_56 (and_56_out, decoder_5_out0, decoder_4_out0);
  and and_57 (and_57_out, and_56_out, and_54_out);
  and and_58 (and_58_out, and_56_out, and_55_out);
  and and_59 (and_59_out, decoder_5_out0, decoder_4_out1);
  and and_60 (and_60_out, and_59_out, and_54_out);
  and and_61 (and_61_out, and_59_out, and_55_out);
  and and_62 (and_62_out, decoder_5_out0, decoder_4_out2);
  and and_63 (and_63_out, and_62_out, and_54_out);
  and and_64 (and_64_out, and_62_out, and_55_out);
  and and_65 (and_65_out, decoder_5_out0, decoder_4_out3);
  and and_66 (and_66_out, and_65_out, and_54_out);
  and and_67 (and_67_out, and_65_out, and_55_out);
  RAM #(.addrWidth(24), .clearpin("true"), .dataWidth(64)) ram_17 (
    .addr(multiplexer_1_out_2), .we(and_57_out), .oe(and_58_out), .clk(Reloj), .din(or_1_out),
    .dout(ram_17_dout), .clr(Limpiar));
  RAM #(.addrWidth(24), .clearpin("true"), .dataWidth(64)) ram_18 (
    .addr(multiplexer_1_out_2), .we(and_60_out), .oe(and_61_out), .clk(Reloj), .din(or_1_out),
    .dout(ram_18_dout), .clr(Limpiar));
  RAM #(.addrWidth(24), .clearpin("true"), .dataWidth(64)) ram_19 (
    .addr(multiplexer_1_out_2), .we(and_63_out), .oe(and_64_out), .clk(Reloj), .din(or_1_out),
    .dout(ram_19_dout), .clr(Limpiar));
  RAM #(.addrWidth(24), .clearpin("true"), .dataWidth(64)) ram_20 (
    .addr(multiplexer_1_out_2), .we(and_66_out), .oe(and_67_out), .clk(Reloj), .din(or_1_out),
    .dout(ram_20_dout), .clr(Limpiar));
  assign controlled_buffer_18_out = and_56_out ? ram_17_dout : 64'bz;  // Controlled_Buffer controlled_buffer_18
  assign controlled_buffer_18_out = and_59_out ? ram_18_dout : 64'bz;  // Controlled_Buffer controlled_buffer_19
  assign controlled_buffer_18_out = and_62_out ? ram_19_dout : 64'bz;  // Controlled_Buffer controlled_buffer_20
  assign controlled_buffer_18_out = and_65_out ? ram_20_dout : 64'bz;  // Controlled_Buffer controlled_buffer_21
  assign Doubleword = decoder_1_out1 ? controlled_buffer_18_out : 64'bz;  // Controlled_Buffer controlled_buffer_22
  and and_68 (and_68_out, decoder_5_out1, decoder_4_out0);
  and and_69 (and_69_out, decoder_5_out1, decoder_4_out1);
  and and_70 (and_70_out, decoder_5_out1, decoder_4_out2);
  and and_71 (and_71_out, decoder_5_out1, decoder_4_out3);
  and and_72 (and_72_out, and_68_out, and_54_out);
  and and_73 (and_73_out, and_68_out, and_55_out);
  and and_74 (and_74_out, and_69_out, and_54_out);
  and and_75 (and_75_out, and_69_out, and_55_out);
  and and_76 (and_76_out, and_70_out, and_54_out);
  and and_77 (and_77_out, and_70_out, and_55_out);
  and and_78 (and_78_out, and_71_out, and_54_out);
  and and_79 (and_79_out, and_71_out, and_55_out);
  RAM #(.addrWidth(24), .clearpin("true"), .dataWidth(64)) ram_21 (
    .addr(multiplexer_1_out_2), .we(and_72_out), .oe(and_73_out), .clk(Reloj), .din(or_1_out),
    .dout(ram_21_dout), .clr(Limpiar));
  RAM #(.addrWidth(24), .clearpin("true"), .dataWidth(64)) ram_22 (
    .addr(multiplexer_1_out_2), .we(and_74_out), .oe(and_75_out), .clk(Reloj), .din(or_1_out),
    .dout(ram_22_dout), .clr(Limpiar));
  RAM #(.addrWidth(24), .clearpin("true"), .dataWidth(64)) ram_23 (
    .addr(multiplexer_1_out_2), .we(and_76_out), .oe(and_77_out), .clk(Reloj), .din(or_1_out),
    .dout(ram_23_dout), .clr(Limpiar));
  RAM #(.addrWidth(24), .clearpin("true"), .dataWidth(64)) ram_24 (
    .addr(multiplexer_1_out_2), .we(and_78_out), .oe(and_79_out), .clk(Reloj), .din(or_1_out),
    .dout(ram_24_dout), .clr(Limpiar));
  assign controlled_buffer_18_out = and_68_out ? ram_21_dout : 64'bz;  // Controlled_Buffer controlled_buffer_23
  assign controlled_buffer_18_out = and_69_out ? ram_22_dout : 64'bz;  // Controlled_Buffer controlled_buffer_24
  assign controlled_buffer_18_out = and_70_out ? ram_23_dout : 64'bz;  // Controlled_Buffer controlled_buffer_25
  assign controlled_buffer_18_out = and_71_out ? ram_24_dout : 64'bz;  // Controlled_Buffer controlled_buffer_26
  and and_80 (and_80_out, decoder_5_out2, decoder_4_out0);
  and and_81 (and_81_out, decoder_5_out2, decoder_4_out1);
  and and_82 (and_82_out, decoder_5_out2, decoder_4_out2);
  and and_83 (and_83_out, decoder_5_out2, decoder_4_out3);
  RAM #(.addrWidth(24), .clearpin("true"), .dataWidth(64)) ram_25 (
    .addr(multiplexer_1_out_2), .we(and_84_out), .oe(and_85_out), .clk(Reloj), .din(or_1_out),
    .dout(ram_25_dout), .clr(Limpiar));
  and and_84 (and_84_out, and_80_out, and_54_out);
  and and_85 (and_85_out, and_80_out, and_55_out);
  RAM #(.addrWidth(24), .clearpin("true"), .dataWidth(64)) ram_26 (
    .addr(multiplexer_1_out_2), .we(and_86_out), .oe(and_87_out), .clk(Reloj), .din(or_1_out),
    .dout(ram_26_dout), .clr(Limpiar));
  and and_86 (and_86_out, and_81_out, and_54_out);
  and and_87 (and_87_out, and_81_out, and_55_out);
  RAM #(.addrWidth(24), .clearpin("true"), .dataWidth(64)) ram_27 (
    .addr(multiplexer_1_out_2), .we(and_88_out), .oe(and_89_out), .clk(Reloj), .din(or_1_out),
    .dout(ram_27_dout), .clr(Limpiar));
  and and_88 (and_88_out, and_82_out, and_54_out);
  and and_89 (and_89_out, and_82_out, and_55_out);
  RAM #(.addrWidth(24), .clearpin("true"), .dataWidth(64)) ram_28 (
    .addr(multiplexer_1_out_2), .we(and_90_out), .oe(and_91_out), .clk(Reloj), .din(or_1_out),
    .dout(ram_28_dout), .clr(Limpiar));
  and and_90 (and_90_out, and_83_out, and_54_out);
  and and_91 (and_91_out, and_83_out, and_55_out);
  and and_92 (and_92_out, decoder_5_out3, decoder_4_out0);
  assign controlled_buffer_18_out = and_80_out ? ram_25_dout : 64'bz;  // Controlled_Buffer controlled_buffer_27
  and and_93 (and_93_out, decoder_5_out3, decoder_4_out1);
  assign controlled_buffer_18_out = and_81_out ? ram_26_dout : 64'bz;  // Controlled_Buffer controlled_buffer_28
  and and_94 (and_94_out, decoder_5_out3, decoder_4_out2);
  assign controlled_buffer_18_out = and_82_out ? ram_27_dout : 64'bz;  // Controlled_Buffer controlled_buffer_29
  and and_95 (and_95_out, decoder_5_out3, decoder_4_out3);
  assign controlled_buffer_18_out = and_83_out ? ram_28_dout : 64'bz;  // Controlled_Buffer controlled_buffer_30
  and and_96 (and_96_out, and_92_out, and_54_out);
  and and_97 (and_97_out, and_92_out, and_55_out);
  and and_98 (and_98_out, and_93_out, and_54_out);
  and and_99 (and_99_out, and_93_out, and_55_out);
  and and_100 (and_100_out, and_94_out, and_54_out);
  and and_101 (and_101_out, and_94_out, and_55_out);
  and and_102 (and_102_out, and_95_out, and_54_out);
  and and_103 (and_103_out, and_95_out, and_55_out);
  RAM #(.addrWidth(24), .clearpin("true"), .dataWidth(64)) ram_29 (
    .addr(multiplexer_1_out_2), .we(and_96_out), .oe(and_97_out), .clk(Reloj), .din(or_1_out),
    .dout(ram_29_dout), .clr(Limpiar));
  RAM #(.addrWidth(24), .clearpin("true"), .dataWidth(64)) ram_30 (
    .addr(multiplexer_1_out_2), .we(and_98_out), .oe(and_99_out), .clk(Reloj), .din(or_1_out),
    .dout(ram_30_dout), .clr(Limpiar));
  RAM #(.addrWidth(24), .clearpin("true"), .dataWidth(64)) ram_31 (
    .addr(multiplexer_1_out_2), .we(and_100_out), .oe(and_101_out), .clk(Reloj), .din(or_1_out),
    .dout(ram_31_dout), .clr(Limpiar));
  RAM #(.addrWidth(24), .clearpin("true"), .dataWidth(64)) ram_32 (
    .addr(multiplexer_1_out_2), .we(and_102_out), .oe(and_103_out), .clk(Reloj), .din(or_1_out),
    .dout(ram_32_dout), .clr(Limpiar));
  assign controlled_buffer_18_out = and_92_out ? ram_29_dout : 64'bz;  // Controlled_Buffer controlled_buffer_31
  assign controlled_buffer_18_out = and_93_out ? ram_30_dout : 64'bz;  // Controlled_Buffer controlled_buffer_32
  assign controlled_buffer_18_out = and_94_out ? ram_31_dout : 64'bz;  // Controlled_Buffer controlled_buffer_33
  assign controlled_buffer_18_out = and_95_out ? ram_32_dout : 64'bz;  // Controlled_Buffer controlled_buffer_34

  // Notes on the sheet:
  //   Tamaño de memoria accesible
  //   Longitud de byte
  //   (Little Endian)
  //   (Big Endian)
  //   2 Gigabytes
  //   2 Gigabytes
endmodule
